# Fritzing sketch Projeto 02 (saved by Fritzing 0.9.5d)
circuit board: 8.46667cm x 5.64444cm
breadboards: 1

parts:
  Componente1 = Arduino Uno (Rev3)
  LED1 = LED - 5mm [color="Red (633nm)" package="5 mm [THT]"]
  LED2 = LED - 5mm [color="Yellow (595nm)" package="5 mm [THT]"]
  LED3 = LED - 5mm [color="Green (565nm)" package="5 mm [THT]"]
  R1 = Resistor [tolerance=±5% resistance=220 package=THT]
  R2 = Resistor [tolerance=±5% resistance=220 package=THT]
  R3 = Resistor [tolerance=±5% resistance=220 package=THT]

nets:
  N1: Componente1.D12/MISO, LED2.anode
  N2: Componente1.D13/SCK, LED1.anode
  N3: Componente1.GND, R1.Pin_0, R2.Pin_0, R3.Pin_0
  N4: Componente1.D2, LED3.anode
  N5: LED1.cathode, R1.Pin_1
  N6: LED2.cathode, R2.Pin_1
  N7: LED3.cathode, R3.Pin_1

// code stored in the sketch: Untitled2.ino
void setup()
{
  pinMode(LED_BUILTIN, OUTPUT);
  pinMode(2,OUTPUT);
  pinMode(12,OUTPUT);
}

void loop()
{
  digitalWrite(LED_BUILTIN, HIGH);
  delay(1000); // Wait for 1000 millisecond(s)
  digitalWrite(LED_BUILTIN, LOW);
  // Wait for 1000 millisecond(s)
 
  digitalWrite(12, HIGH);
  delay(1000); // Wait for 1000 millisecond(s)
  digitalWrite(12, LOW);
  
  digitalWrite(2, HIGH);
  delay(1000);
  digitalWrite(2, LOW);
}
