# Fritzing sketch Projeto 03 (saved by Fritzing 0.9.5d)
breadboards: 1

parts:
  Componente1 = Arduino Uno (Rev3)
  R1 = Resistor [tolerance=±5% resistance=220 package=THT]
  LED1 = LED - 5mm [color="Red (633nm)" package="5 mm [THT]"]
  S1 = Pushbutton [package="[THT]"]
  R2 = Resistor [tolerance=±5% resistance=220 package=THT]

nets:
  N1: Componente1.D8, LED1.anode
  N2: Componente1.D12/MISO, S1.Pin_1, S1.Pin_2, R2.Pin_1
  N3: Componente1.5V, R2.Pin_0
  N4: Componente1.GND, R1.Pin_0, S1.Pin_3, S1.Pin_4
  N5: R1.Pin_1, LED1.cathode

// code stored in the sketch: Untitled3.ino
int LED = 8;
int Button = 12;
int ValEntrada = LOW;
void setup(){
  pinMode(LED, OUTPUT);
  pinMode(Button, INPUT);
}

void loop() {
  ValEntrada = digitalRead (Button);
  if (ValEntrada == HIGH){
    digitalWrite(LED, LOW);
  }
  else{
    digitalWrite(LED, HIGH);
  }
  delay(100);
}
