# Fritzing sketch Projeto 04 (saved by Fritzing 0.9.5d)
circuit board: 8.46667cm x 5.64444cm
breadboards: 1

parts:
  Componente1 = Arduino Uno (Rev3)
  LED1 = LED - 5mm [color="Red (633nm)" package="5 mm [THT]"]
  R1 = Resistor [tolerance=±5% resistance=220 package=THT]

nets:
  N1: Componente1.D9_PWM, LED1.anode
  N2: Componente1.GND, R1.Pin_0
  N3: LED1.cathode, R1.Pin_1

// code stored in the sketch: Untitled4.ino
int LED = 9;
int i = 0;
void setup() {
  pinMode (LED,OUTPUT);
}
void loop() {
  for (i = 0; i < 255; i++) {
    analogWrite (LED,i);
    delay(10);
  }
  for (i = 255; i >= 0; i--) {
     analogWrite (LED,i);
    delay(10);
  }
}
