# Fritzing sketch Projeto 05 (saved by Fritzing 0.9.5d)
breadboards: 1

parts:
  Componente1 = Arduino Uno (Rev3)
  LED1 = LED - 5mm [color="Red (633nm)" package="5 mm [THT]"]
  R1 = Resistor [tolerance=±5% resistance=220 package=THT]
  R2 = Rotary Potentiometer (Small) [maximum_resistance=100kΩ package=THT]

nets:
  N1: Componente1.A1, R2.wiper
  N2: Componente1.D13/SCK, LED1.anode
  N3: Componente1.5V, R2.leg2
  N4: Componente1.GND, R1.Pin_0, R2.leg1
  N5: LED1.cathode, R1.Pin_1

// code stored in the sketch: Untitled7.ino
int POT = A1;
int LED = 13;
int valor = 0;

void setup() {
  pinMode(LED, OUTPUT);
  pinMode(POT, INPUT);
}

void loop() {
  valor = analogRead(POT);
  digitalWrite(LED, HIGH);
  delay(valor);
  digitalWrite(LED, LOW);
  delay(valor);
  
}
