# Fritzing sketch Projeto 07 (saved by Fritzing 0.9.5d)
breadboards: 1

parts:
  Componente1 = Arduino Uno (Rev3)
  LED1 = LED - 5mm [color="Red (633nm)" package="5 mm [THT]"]
  R1 = Resistor [tolerance=±5% resistance=220 package=THT]
  S1 = Pushbutton [package="[THT]"]
  R2 = Resistor [tolerance=±5% resistance=220 package=THT]

nets:
  N1: Componente1.D9_PWM, S1.Pin_1, S1.Pin_2, R2.Pin_1
  N2: Componente1.D7, LED1.anode
  N3: Componente1.5V, S1.Pin_3, S1.Pin_4
  N4: Componente1.GND, R1.Pin_0, R2.Pin_0
  N5: LED1.cathode, R1.Pin_1

// code stored in the sketch: Untitled10.ino
int LED = 9; 
int BOTAO = 7;
int valor = LOW; 
int valorAnterior = LOW;
int estado = 0; 
int brilho = 128; 
unsigned long inicio;

void setup() {
  pinMode (LED, OUTPUT); 
}

void loop() {
  valor = digitalRead (BOTAO);
  if ((valor == HIGH) && (valorAnterior == LOW)) { 
    estado = 1 - estado;
    inicio = millis();
    delay (10);
  }
  if ((valor == HIGH) && (valorAnterior == HIGH)) {
    if (estado == 1 && (millis() - inicio) > 500) {
      brilho++;
      delay(10);
      if (brilho > 255)
        brilho = 0;
    }
  }
  valorAnterior = valor;
  if (estado == 1)
    analogWrite (LED, brilho); 
  else
    analogWrite(LED, 0); 
}
