# Fritzing sketch Projeto 08 (saved by Fritzing 0.9.5d)
breadboards: 1

parts:
  LED1 = RGB LED (com. cathode, rgb) [package="5 mm [THT]"]
  Componente1 = Arduino Uno (Rev3)
  R1 = Resistor [tolerance=±5% resistance=220 package=THT]
  R2 = Resistor [tolerance=±5% resistance=220 package=THT]
  R3 = Resistor [tolerance=±5% resistance=220 package=THT]

nets:
  N1: LED1.red_anode, R2.Pin_1
  N2: LED1.common_cathode, Componente1.GND
  N3: LED1.green_anode, R3.Pin_1
  N4: LED1.blue_anode, R1.Pin_1
  N5: Componente1.D9_PWM, R2.Pin_0
  N6: Componente1.D10_PWM/SS, R3.Pin_0
  N7: Componente1.D11_PWM/MOSI, R1.Pin_0

// code stored in the sketch: Untitled11.ino
int VERMELHO = 9;
int VERDE = 10;
int AZUL = 11;

int iVermelho = 0;
int iVerde = 0;
int iAzul = 0;

void setup()
{pinMode (VERMELHO, OUTPUT); 
 pinMode (VERDE, OUTPUT); 
 pinMode (AZUL, OUTPUT);
}

void loop()
{analogWrite (VERMELHO, iVermelho); 
 analogWrite (VERDE, iVerde); 
 analogWrite (AZUL, iAzul);
 delay(500);
 
 iVermelho = random (256);
 iVerde = random (256);
 iAzul = random (256);
}
